# Fritzing sketch Wiring (saved by Fritzing 0.9.2b)
perfboards: 1

parts:
  UDN_2981_-_8-Channel_Source_Driver1 = DIP - 18 pins [package="DIP (Dual Inline) [THT]"]
  U1 = Header 1 [package=1x01_offset]
  U2 = Header 1 [package=1x01_offset]
  VCC1 = Battery block 9V
  U3 = Header 1 [package=1x01_offset]
  U4 = Header 1 [package=1x01_offset]
  Bauteil1 = Dual H-Bridge L298
  U5 = Header 1 [package=1x01_offset]
  U6 = Header 1 [package=1x01_offset]
  U7 = Header 1 [package=1x01_offset]
  U8 = Header 1 [package=1x01_offset]
  U9 = Header 1 [package=1x01_offset]
  U10 = Header 1 [package=1x01_offset]
  U11 = Header 1 [package=1x01_offset]
  U12 = Header 1 [package=1x01_offset]
  U13 = Header 1 [package=1x01_offset]
  U14 = Header 1 [package=1x01_offset]
  U15 = Header 1 [package=1x01_offset]
  U16 = Header 1 [package=1x01_offset]
  U17 = Header 1 [package=1x01_offset]
  U18 = Header 1 [package=1x01_offset]
  U19 = Header 1 [package=1x01_offset]
  U20 = Header 1 [package=1x01_offset]
  U21 = Header 1 [package=1x01_offset]
  U22 = Header 1 [package=1x01_offset]
  U23 = Header 1 [package=1x01_offset]
  J1 = Basic Servo
  U24 = Header 1 [package=1x01_offset]
  U25 = Header 1 [package=1x01_offset]
  U26 = Header 1 [package=1x01_offset]
  U27 = Header 1 [package=1x01_offset]
  U28 = Header 1 [package=1x01_offset]
  U29 = Header 1 [package=1x01_offset]
  U30 = Header 1 [package=1x01_offset]
  U31 = Header 1 [package=1x01_offset]
  U32 = Header 1 [package=1x01_offset]
  U33 = Header 1 [package=1x01_offset]
  U34 = Header 1 [package=1x01_offset]
  U35 = Header 1 [package=1x01_offset]
  M1 = DC Motor
  U36 = Header 1 [package=1x01_offset]
  U37 = Header 1 [package=1x01_offset]
  U38 = Header 1 [package=1x01_offset]
  U39 = Header 1 [package=1x01_offset]
  U40 = Header 1 [package=1x01_offset]
  U41 = Header 1 [package=1x01_offset]
  U42 = Header 1 [package=1x01_offset]
  U43 = Header 1 [package=1x01_offset]
  R12 = Resistor [tolerance=±5% resistance=1k package="1206 [SMD]"]
  R14 = Resistor [tolerance=±5% resistance=1k package="1206 [SMD]"]
  R16 = Resistor [tolerance=±5% resistance=1k package="1206 [SMD]"]
  R17 = Resistor [tolerance=±5% resistance=1k package="1206 [SMD]"]
  R18 = Resistor [tolerance=±5% resistance=1k package="1206 [SMD]"]
  R19 = Resistor [tolerance=±5% resistance=1k package="1206 [SMD]"]
  R20 = Resistor [tolerance=±5% resistance=1k package="1206 [SMD]"]
  R21 = Resistor [tolerance=±5% resistance=1k package="1206 [SMD]"]
  R22 = Resistor [tolerance=±5% resistance=1k package="1206 [SMD]"]
  R23 = Resistor [tolerance=±5% resistance=1k package="1206 [SMD]"]
  R24 = Resistor [tolerance=±5% resistance=1k package="1206 [SMD]"]

nets:
  N1: UDN_2981_-_8-Channel_Source_Driver1.In_1, U27.1
  N2: UDN_2981_-_8-Channel_Source_Driver1.In_2, U26.1
  N3: UDN_2981_-_8-Channel_Source_Driver1.In_3, U25.1
  N4: UDN_2981_-_8-Channel_Source_Driver1.In_4, U32.1
  N5: UDN_2981_-_8-Channel_Source_Driver1.In_5, U24.1
  N6: UDN_2981_-_8-Channel_Source_Driver1.In_6, U33.1
  N7: UDN_2981_-_8-Channel_Source_Driver1.In_7, U31.1
  N8: UDN_2981_-_8-Channel_Source_Driver1.In_8, U34.1
  VCC: UDN_2981_-_8-Channel_Source_Driver1.Vcc, Bauteil1.5V, Bauteil1.+5V, U5.1, U22.1, J1.vcc
  GND: UDN_2981_-_8-Channel_Source_Driver1.GND, U2.1, VCC1.-, U4.1, Bauteil1.GND, U9.1, U10.1, U11.1, U12.1, U13.1, U14.1, U15.1, U16.1, U18.1, U21.1, J1.gnd, U35.1
  N9: UDN_2981_-_8-Channel_Source_Driver1.Out_8, R23.Pin_0
  N10: UDN_2981_-_8-Channel_Source_Driver1.Out_7, R22.Pin_0
  N11: UDN_2981_-_8-Channel_Source_Driver1.Out_6, R21.Pin_0
  N12: UDN_2981_-_8-Channel_Source_Driver1.Out_5, R19.Pin_0, R20.Pin_0
  N13: UDN_2981_-_8-Channel_Source_Driver1.Out_4, R17.Pin_0, R18.Pin_0
  N14: UDN_2981_-_8-Channel_Source_Driver1.Out_3, R16.Pin_0, R24.Pin_0
  N15: UDN_2981_-_8-Channel_Source_Driver1.Out_2, R12.Pin_0
  N16: UDN_2981_-_8-Channel_Source_Driver1.Out_1, U23.1, J1.pulse
  N17: U1.1, VCC1.+, U3.1, Bauteil1.VMS
  N18: Bauteil1.MOTORA1, M1.pin_1
  N19: Bauteil1.MOTORA2, M1.pin_2
  N20: Bauteil1.ENA, U6.1, U30.1
  N21: Bauteil1.IN1, U7.1, U29.1
  N22: Bauteil1.IN2, U8.1, U28.1
  N23: U17.1, R21.Pin_1
  N24: U19.1, R22.Pin_1
  N25: U20.1, R23.Pin_1
  N26: U36.1, R20.Pin_1
  N27: U37.1, R19.Pin_1
  N28: U38.1, R18.Pin_1
  N29: U39.1, R17.Pin_1
  N30: U40.1, R16.Pin_1
  N31: U41.1, R24.Pin_1
  N32: U42.1, R14.Pin_1
  N33: U43.1, R12.Pin_1

custom parts:
  DIP - 18 pins: Recommended for high-side switching applications that benefit from separate logic and load grounds, these devices encompass load supply voltages to 50 V and output currents to -500 mA. These 8-channel source drivers are useful for interfacing between low-level logic and high-current loads. Typical loads include relays, solenoids, lamps, stepper and/or servo motors, print hammers, and LEDs.
  Dual H-Bridge L298: Description:The L298N driver module, using ST's L298N chip can directly drive two 3-30V DC motor, and provides a 5V output interface can 5V single-chip circuitry to supply, support 3.3VMCU control, you can easily control the DC motor speed and direction, you can also control the 2-phase stepper motor, smart car essential. Features: Driver: L298N Dual H Bridge DC Motor Driver IC Driven part of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
